// Logisim project 16 bit register file.circ as structural Verilog: 3 circuits, main circuit main
module main (
  input  [15:0] Write_Data,
  input  [3:0] Write_Register,
  input  in_3,
  input  [3:0] Read_Register_2,
  input  [3:0] Read_Register_1,
  input  CLK,
  output [15:0] Read_Data_1,
  output [15:0] Read_Data_2
);

  Register_File register_file_1 (
    .Write_Data(Write_Data), .Write(in_3), .CLK(CLK), .Read_Register_1(Read_Register_1),
    .Read_Register_2(Read_Register_2), .Read_Data_1(Read_Data_1), .Read_Data_2(Read_Data_2),
    .Write_Register(Write_Register));
endmodule

module _16_bit_register (
  input  CLK,
  input  [15:0] in_2,
  input  in_3,
  output [15:0] out_4
);

  D_Flip_Flop d_ff_1 (.clk(CLK), .D(in_2[0]), .Q(out_4[0]), .en(in_3));  // open: Qn, preset, reset
  D_Flip_Flop d_ff_2 (.clk(CLK), .D(in_2[1]), .Q(out_4[1]), .en(in_3));  // open: Qn, preset, reset
  D_Flip_Flop d_ff_3 (.clk(CLK), .D(in_2[2]), .Q(out_4[2]), .en(in_3));  // open: Qn, preset, reset
  D_Flip_Flop d_ff_4 (.clk(CLK), .D(in_2[3]), .Q(out_4[3]), .en(in_3));  // open: Qn, preset, reset
  D_Flip_Flop d_ff_5 (.clk(CLK), .D(in_2[4]), .Q(out_4[4]), .en(in_3));  // open: Qn, preset, reset
  D_Flip_Flop d_ff_6 (.clk(CLK), .D(in_2[5]), .Q(out_4[5]), .en(in_3));  // open: Qn, preset, reset
  D_Flip_Flop d_ff_7 (.clk(CLK), .D(in_2[6]), .Q(out_4[6]), .en(in_3));  // open: Qn, preset, reset
  D_Flip_Flop d_ff_8 (.clk(CLK), .D(in_2[7]), .Q(out_4[7]), .en(in_3));  // open: Qn, preset, reset
  D_Flip_Flop d_ff_9 (.clk(CLK), .D(in_2[8]), .Q(out_4[8]), .en(in_3));  // open: Qn, preset, reset
  D_Flip_Flop d_ff_10 (.clk(CLK), .D(in_2[9]), .Q(out_4[9]), .en(in_3));  // open: Qn, preset, reset
  D_Flip_Flop d_ff_11 (.clk(CLK), .D(in_2[10]), .Q(out_4[10]), .en(in_3));  // open: Qn, preset, reset
  D_Flip_Flop d_ff_12 (.clk(CLK), .D(in_2[11]), .Q(out_4[11]), .en(in_3));  // open: Qn, preset, reset
  D_Flip_Flop d_ff_13 (.clk(CLK), .D(in_2[12]), .Q(out_4[12]), .en(in_3));  // open: Qn, preset, reset
  D_Flip_Flop d_ff_14 (.clk(CLK), .D(in_2[13]), .Q(out_4[13]), .en(in_3));  // open: Qn, preset, reset
  D_Flip_Flop d_ff_15 (.clk(CLK), .D(in_2[14]), .Q(out_4[14]), .en(in_3));  // open: Qn, preset, reset
  D_Flip_Flop d_ff_16 (.clk(CLK), .D(in_2[15]), .Q(out_4[15]), .en(in_3));  // open: Qn, preset, reset
endmodule

module Register_File (
  input  [15:0] Write_Data,
  input  [3:0] Read_Register_1,
  input  [3:0] Read_Register_2,
  input  CLK,
  input  [3:0] Write_Register,
  input  Write,
  output [15:0] Read_Data_1,
  output [15:0] Read_Data_2
);

  wire decoder_1_out0, decoder_1_out1, decoder_1_out2, decoder_1_out3, decoder_1_out4, decoder_1_out5,
       decoder_1_out6, decoder_1_out7, decoder_1_out8, decoder_1_out9, decoder_1_out10, decoder_1_out11,
       decoder_1_out12, decoder_1_out13, decoder_1_out14, decoder_1_out15;
  wire [15:0] n16_bit_register_1_out_4, n16_bit_register_2_out_4, n16_bit_register_3_out_4,
       n16_bit_register_4_out_4, n16_bit_register_5_out_4, n16_bit_register_6_out_4,
       n16_bit_register_7_out_4, n16_bit_register_8_out_4, n16_bit_register_9_out_4,
       n16_bit_register_10_out_4, n16_bit_register_11_out_4, n16_bit_register_12_out_4,
       n16_bit_register_13_out_4, n16_bit_register_14_out_4, n16_bit_register_15_out_4,
       n16_bit_register_16_out_4;

  Decoder #(.select(4)) decoder_1 (
    .out0(decoder_1_out0), .out1(decoder_1_out1), .out2(decoder_1_out2), .out3(decoder_1_out3),
    .out4(decoder_1_out4), .out5(decoder_1_out5), .out6(decoder_1_out6), .out7(decoder_1_out7),
    .out8(decoder_1_out8), .out9(decoder_1_out9), .out10(decoder_1_out10), .out11(decoder_1_out11),
    .out12(decoder_1_out12), .out13(decoder_1_out13), .out14(decoder_1_out14), .out15(decoder_1_out15),
    .sel(Write_Register), .en(Write));
  _16_bit_register u_16_bit_register_1 (
    .CLK(CLK), .in_2(Write_Data), .out_4(n16_bit_register_1_out_4), .in_3(decoder_1_out0));
  _16_bit_register u_16_bit_register_2 (
    .CLK(CLK), .in_2(Write_Data), .out_4(n16_bit_register_2_out_4), .in_3(decoder_1_out1));
  _16_bit_register u_16_bit_register_3 (
    .CLK(CLK), .in_2(Write_Data), .out_4(n16_bit_register_3_out_4), .in_3(decoder_1_out2));
  _16_bit_register u_16_bit_register_4 (
    .CLK(CLK), .in_2(Write_Data), .out_4(n16_bit_register_4_out_4), .in_3(decoder_1_out3));
  _16_bit_register u_16_bit_register_5 (
    .CLK(CLK), .in_2(Write_Data), .out_4(n16_bit_register_5_out_4), .in_3(decoder_1_out4));
  _16_bit_register u_16_bit_register_6 (
    .CLK(CLK), .in_2(Write_Data), .out_4(n16_bit_register_6_out_4), .in_3(decoder_1_out5));
  _16_bit_register u_16_bit_register_7 (
    .CLK(CLK), .in_2(Write_Data), .out_4(n16_bit_register_7_out_4), .in_3(decoder_1_out6));
  _16_bit_register u_16_bit_register_8 (
    .CLK(CLK), .in_2(Write_Data), .out_4(n16_bit_register_8_out_4), .in_3(decoder_1_out7));
  _16_bit_register u_16_bit_register_9 (
    .CLK(CLK), .in_2(Write_Data), .out_4(n16_bit_register_9_out_4), .in_3(decoder_1_out8));
  _16_bit_register u_16_bit_register_10 (
    .CLK(CLK), .in_2(Write_Data), .out_4(n16_bit_register_10_out_4), .in_3(decoder_1_out9));
  _16_bit_register u_16_bit_register_11 (
    .CLK(CLK), .in_2(Write_Data), .out_4(n16_bit_register_11_out_4), .in_3(decoder_1_out10));
  _16_bit_register u_16_bit_register_12 (
    .CLK(CLK), .in_2(Write_Data), .out_4(n16_bit_register_12_out_4), .in_3(decoder_1_out11));
  _16_bit_register u_16_bit_register_13 (
    .CLK(CLK), .in_2(Write_Data), .out_4(n16_bit_register_13_out_4), .in_3(decoder_1_out12));
  _16_bit_register u_16_bit_register_14 (
    .CLK(CLK), .in_2(Write_Data), .out_4(n16_bit_register_14_out_4), .in_3(decoder_1_out13));
  _16_bit_register u_16_bit_register_15 (
    .CLK(CLK), .in_2(Write_Data), .out_4(n16_bit_register_15_out_4), .in_3(decoder_1_out14));
  _16_bit_register u_16_bit_register_16 (
    .CLK(CLK), .in_2(Write_Data), .out_4(n16_bit_register_16_out_4), .in_3(decoder_1_out15));
  Multiplexer #(.select(4), .width(16)) multiplexer_1 (
    .in0(n16_bit_register_1_out_4), .in1(n16_bit_register_2_out_4), .in2(n16_bit_register_3_out_4),
    .in3(n16_bit_register_4_out_4), .in4(n16_bit_register_5_out_4), .in5(n16_bit_register_6_out_4),
    .in6(n16_bit_register_7_out_4), .in7(n16_bit_register_8_out_4), .in8(n16_bit_register_9_out_4),
    .in9(n16_bit_register_10_out_4), .in10(n16_bit_register_11_out_4), .in11(n16_bit_register_12_out_4),
    .in12(n16_bit_register_13_out_4), .in13(n16_bit_register_14_out_4), .in14(n16_bit_register_15_out_4),
    .in15(n16_bit_register_16_out_4), .out(Read_Data_1), .sel(Read_Register_1));  // open: en
  Multiplexer #(.select(4), .width(16)) multiplexer_2 (
    .in0(n16_bit_register_1_out_4), .in1(n16_bit_register_2_out_4), .in2(n16_bit_register_3_out_4),
    .in3(n16_bit_register_4_out_4), .in4(n16_bit_register_5_out_4), .in5(n16_bit_register_6_out_4),
    .in6(n16_bit_register_7_out_4), .in7(n16_bit_register_8_out_4), .in8(n16_bit_register_9_out_4),
    .in9(n16_bit_register_10_out_4), .in10(n16_bit_register_11_out_4), .in11(n16_bit_register_12_out_4),
    .in12(n16_bit_register_13_out_4), .in13(n16_bit_register_14_out_4), .in14(n16_bit_register_15_out_4),
    .in15(n16_bit_register_16_out_4), .out(Read_Data_2), .sel(Read_Register_2));  // open: en
endmodule
