// Logisim project 8 bit Logic Unit with operation AND, NAND, OR, NOR, XOR, XNOR, ANOT, BNOT..circ as structural Verilog: 1 circuit, main circuit main
module main (
  input  A0,
  input  B0,
  input  A1,
  input  [2:0] in_4,
  input  B1,
  input  A2,
  input  B2,
  input  A3,
  input  B3,
  input  A4,
  input  B4,
  input  A5,
  input  B5,
  input  A6,
  input  B6,
  input  A7,
  input  B7,
  output F0,
  output F1,
  output F2,
  output F3,
  output F4,
  output F5,
  output F6,
  output F7
);

  wire and_1_out, and_2_out, and_3_out, and_4_out, and_5_out, and_6_out, and_7_out, and_8_out, nand_1_out,
       nand_2_out, nand_3_out, nand_4_out, nand_5_out, nand_6_out, nand_7_out, nand_8_out, nor_1_out,
       nor_2_out, nor_3_out, nor_4_out, nor_5_out, nor_6_out, nor_7_out, nor_8_out, not_1_out, not_2_out,
       not_3_out, not_4_out, not_5_out, not_6_out, not_7_out, not_8_out, not_9_out, not_10_out, not_11_out,
       not_12_out, not_13_out, not_15_out, not_16_out, or_1_out, or_2_out, or_3_out, or_4_out, or_5_out,
       or_6_out, or_7_out, or_8_out, xnor_1_out, xnor_2_out, xnor_3_out, xnor_4_out, xnor_5_out, xnor_6_out,
       xnor_7_out, xnor_8_out, xor_1_out, xor_2_out, xor_3_out, xor_4_out, xor_5_out, xor_6_out, xor_7_out,
       xor_8_out;

  and and_1 (and_1_out, A0, B0);
  nand nand_1 (nand_1_out, A0, B0);
  or or_1 (or_1_out, A0, B0);
  nor nor_1 (nor_1_out, A0, B0);
  xor xor_1 (xor_1_out, A0, B0);
  xnor xnor_1 (xnor_1_out, A0, B0);
  not not_1 (not_1_out, A0);
  not not_2 (not_2_out, B0);
  and and_2 (and_2_out, A1, B1);
  nand nand_2 (nand_2_out, A1, B1);
  or or_2 (or_2_out, A1, B1);
  nor nor_2 (nor_2_out, A1, B1);
  xor xor_2 (xor_2_out, A1, B1);
  xnor xnor_2 (xnor_2_out, A1, B1);
  not not_3 (not_3_out, A1);
  not not_4 (not_4_out, B1);
  and and_3 (and_3_out, A2, B2);
  nand nand_3 (nand_3_out, A2, B2);
  or or_3 (or_3_out, A2, B2);
  nor nor_3 (nor_3_out, A2, B2);
  xor xor_3 (xor_3_out, A2, B2);
  xnor xnor_3 (xnor_3_out, A2, B2);
  not not_5 (not_5_out, A2);
  not not_6 (not_6_out, B2);
  and and_4 (and_4_out, A3, B3);
  nand nand_4 (nand_4_out, A3, B3);
  or or_4 (or_4_out, A3, B3);
  nor nor_4 (nor_4_out, A3, B3);
  xor xor_4 (xor_4_out, A3, B3);
  xnor xnor_4 (xnor_4_out, A3, B3);
  not not_7 (not_7_out, A3);
  not not_8 (not_8_out, B3);
  and and_5 (and_5_out, A4, B4);
  nand nand_5 (nand_5_out, A4, B4);
  or or_5 (or_5_out, A4, B4);
  nor nor_5 (nor_5_out, A4, B4);
  xor xor_5 (xor_5_out, A4, B4);
  xnor xnor_5 (xnor_5_out, A4, B4);
  not not_9 (not_9_out, A4);
  not not_10 (not_10_out, B4);
  and and_6 (and_6_out, A5, A5);
  nand nand_6 (nand_6_out, A5, A5);
  or or_6 (or_6_out, A5, A5);
  nor nor_6 (nor_6_out, A5, A5);
  xor xor_6 (xor_6_out, A5, A5);
  xnor xnor_6 (xnor_6_out, A5, A5);
  not not_11 (not_11_out, A5);
  not not_12 (not_12_out, A5);
  and and_7 (and_7_out, A6, B6);
  nand nand_7 (nand_7_out, A6, B6);
  or or_7 (or_7_out, A6, B6);
  nor nor_7 (nor_7_out, A6, B6);
  xor xor_7 (xor_7_out, A6, B6);
  xnor xnor_7 (xnor_7_out, A6, B6);
  not not_13 (not_13_out, A6);
  // NOT_Gate not_14 has open pins: in=B6, out=open
  and and_8 (and_8_out, A7, B7);
  nand nand_8 (nand_8_out, A7, B7);
  or or_8 (or_8_out, A7, B7);
  nor nor_8 (nor_8_out, A7, B7);
  xor xor_8 (xor_8_out, A7, B7);
  xnor xnor_8 (xnor_8_out, A7, B7);
  not not_15 (not_15_out, A7);
  not not_16 (not_16_out, B7);
  Multiplexer #(.select(3)) multiplexer_1 (
    .in0(and_8_out), .in1(nand_8_out), .in2(or_8_out), .in3(nor_8_out), .in4(xor_8_out), .in5(xnor_8_out),
    .in6(not_15_out), .in7(not_16_out), .out(F7), .sel(in_4));  // open: en
  Multiplexer #(.select(3)) multiplexer_2 (
    .in0(and_1_out), .in1(nand_1_out), .in2(or_1_out), .in3(nor_1_out), .in4(xor_1_out), .in5(xnor_1_out),
    .in6(not_1_out), .in7(not_2_out), .out(F0), .sel(in_4));  // open: en
  Multiplexer #(.select(3)) multiplexer_3 (
    .in0(and_2_out), .in1(nand_2_out), .in2(or_2_out), .in3(nor_2_out), .in4(xor_2_out), .in5(xnor_2_out),
    .in6(not_3_out), .in7(not_4_out), .out(F1), .sel(in_4));  // open: en
  Multiplexer #(.select(3)) multiplexer_4 (
    .in0(and_3_out), .in1(nand_3_out), .in2(or_3_out), .in3(nor_3_out), .in4(xor_3_out), .in5(xnor_3_out),
    .in6(not_5_out), .in7(not_6_out), .out(F2), .sel(in_4));  // open: en
  Multiplexer #(.select(3)) multiplexer_5 (
    .in0(and_4_out), .in1(nand_4_out), .in2(or_4_out), .in3(nor_4_out), .in4(xor_4_out), .in5(xnor_4_out),
    .in6(not_7_out), .in7(not_8_out), .out(F3), .sel(in_4));  // open: en
  Multiplexer #(.select(3)) multiplexer_6 (
    .in0(and_5_out), .in1(nand_5_out), .in2(or_5_out), .in3(nor_5_out), .in4(xor_5_out), .in5(xnor_5_out),
    .in6(not_9_out), .in7(not_10_out), .out(F4), .sel(in_4));  // open: en
  Multiplexer #(.select(3)) multiplexer_7 (
    .in0(and_6_out), .in1(nand_6_out), .in2(or_6_out), .in3(nor_6_out), .in4(xor_6_out), .in5(xnor_6_out),
    .in6(not_11_out), .in7(not_12_out), .out(F5), .sel(in_4));  // open: en
  Multiplexer #(.select(3)) multiplexer_8 (
    .in0(and_7_out), .in1(nand_7_out), .in2(or_7_out), .in3(nor_7_out), .in4(xor_7_out), .in5(xnor_7_out),
    .in6(not_13_out), .out(F6), .sel(in_4));  // open: in7, en

  assign B5 = A5;
endmodule
